# Fritzing sketch Schematic AT-ST (saved by Fritzing 0.9.3b)
breadboards: 1

parts:
  L1 = Basic Servo
  L3 = Basic Servo
  L2 = Basic Servo
  LIPO_1_-_1300_mAh = LIPO-1000mAh [package=lipo-1000]
  LIPO_2_-_1300_mAh = LIPO-1000mAh [package=lipo-1000]
  DC-DC_(5V)_Converter = Breadboard Power Supply Board SMD
  DC-DC_(5V)_Converter_2 = Breadboard Power Supply Board SMD
  C1 = Capacitor Polarized [package=cpol-radial-100uf-25v]
  Battery_Voltage_Tester = Digital Panel Meter, Voltage, DMS-20PC
  Battery_Voltage_Tester_2 = Digital Panel Meter, Voltage, DMS-20PC
  RPI_PWM_Shield = Adafruit 16-Channel PWM + Servo HAT [part_number="Adafruit #2327"]
  Raspberry_Pi_3 = Raspberry Pi 3 [part_number=RPI-3-V1.2]
  L4 = Basic Servo
  R5 = Basic Servo
  R4 = Basic Servo
  R3 = Basic Servo
  R2 = Basic Servo
  Aruino_Nano_1 = Arduino Nano v2.3
  RPI_USB_PORT2 = USB Connectors [package=usb-a-s-silk-female]
  Arduino_1_USB_Port = USB Connectors [package=usb-a-s-silk-female]
  9DOF_Gyroscope_1 = Tri-Axis Gyro Breakout - L3G4200D [part_number=MPU-9150]
  Aruino_Nano_2 = Arduino Nano v2.3
  Arduino_2_USB_Port = USB Connectors [package=usb-a-s-silk-female]
  9DOF_Gyroscope_2 = Tri-Axis Gyro Breakout - L3G4200D [part_number=MPU-9150]
  RPI_USB_PORT1 = USB Connectors [package=usb-a-s-silk-female]
  R1 = Basic Servo
  L5 = Basic Servo

nets:
  GND: L1.gnd, L3.gnd, L2.gnd, LIPO_1_-_1300_mAh.-, DC-DC_(5V)_Converter.GND, Battery_Voltage_Tester.3:_GND, RPI_PWM_Shield.GND, L4.gnd, R5.gnd, R4.gnd, R3.gnd, R2.gnd, R1.gnd, L5.gnd
  VCC: L1.vcc, L3.vcc, L2.vcc, C1.+, L4.vcc, R5.vcc, R4.vcc, R3.vcc, R2.vcc, R1.vcc, L5.vcc
  N1: L1.pulse, RPI_PWM_Shield.#0
  N2: L3.pulse, RPI_PWM_Shield.#2
  N3: L2.pulse, RPI_PWM_Shield.#1
  N4: LIPO_1_-_1300_mAh.+, DC-DC_(5V)_Converter.VIN, Battery_Voltage_Tester.1:_VCC
  N5: LIPO_2_-_1300_mAh.+, DC-DC_(5V)_Converter_2.VIN, Battery_Voltage_Tester_2.1:_VCC
  GND_2: LIPO_2_-_1300_mAh.-, DC-DC_(5V)_Converter_2.GND, Battery_Voltage_Tester_2.3:_GND, Raspberry_Pi_3.GND
  N6: DC-DC_(5V)_Converter.VCC, RPI_PWM_Shield.PWRIN
  VCC_2: DC-DC_(5V)_Converter_2.VCC, Raspberry_Pi_3.5V
  N7: C1.-, RPI_PWM_Shield.+5V
  N8: RPI_PWM_Shield.SDA, Raspberry_Pi_3.GPIO2
  N9: RPI_PWM_Shield.SCL, Raspberry_Pi_3.GPIO3
  N10: RPI_PWM_Shield.#7, R3.pulse
  N11: RPI_PWM_Shield.#6, R2.pulse
  N12: RPI_PWM_Shield.#5, R1.pulse
  N13: RPI_PWM_Shield.#4, L5.pulse
  N14: RPI_PWM_Shield.#3, L4.pulse
  N15: RPI_PWM_Shield.#9, R5.pulse
  N16: RPI_PWM_Shield.#8, R4.pulse
  3.3V: RPI_PWM_Shield.3.3V, Raspberry_Pi_3.3V3
  GND_3: Aruino_Nano_1.GND, 9DOF_Gyroscope_1.GND
  N17: Aruino_Nano_1.D2, 9DOF_Gyroscope_1.INT1
  N18: Aruino_Nano_1.A5, 9DOF_Gyroscope_1.SCL
  N19: Aruino_Nano_1.A4, 9DOF_Gyroscope_1.SDA
  +5V: Aruino_Nano_1.+5V, 9DOF_Gyroscope_1.VCC
  USB Cable 2: Power/Serial: RPI_USB_PORT2.D+, RPI_USB_PORT2.D-, RPI_USB_PORT2.GND, RPI_USB_PORT2.VBUS
  N20: Arduino_1_USB_Port.D+, Arduino_1_USB_Port.D-, Arduino_1_USB_Port.GND, Arduino_1_USB_Port.VBUS
  GND_4: Aruino_Nano_2.GND, 9DOF_Gyroscope_2.GND
  N21: Aruino_Nano_2.D2, 9DOF_Gyroscope_2.INT1
  N22: Aruino_Nano_2.A5, 9DOF_Gyroscope_2.SCL
  N23: Aruino_Nano_2.A4, 9DOF_Gyroscope_2.SDA
  +5V_2: Aruino_Nano_2.+5V, 9DOF_Gyroscope_2.VCC
  N24: Arduino_2_USB_Port.D+, Arduino_2_USB_Port.D-, Arduino_2_USB_Port.GND, Arduino_2_USB_Port.VBUS
  USB Cable 1: Power/Serial: RPI_USB_PORT1.D+, RPI_USB_PORT1.D-, RPI_USB_PORT1.GND, RPI_USB_PORT1.VBUS

custom parts:
  Adafruit 16-Channel PWM + Servo HAT: The Raspberry Pi is a wonderful little computer, but one thing it isn't very good at is controlling DC Servo Motors - these motors need very specific and repetitive timing pulses to set the position. Instead of asking the Pi Linux kernel to send these signals, pop on this handy HAT! It adds the capability to control 16 Servos with perfect timing. It can also do PWM up to 1.6 KHz with 12 bit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
